# Fritzing sketch WiringSketch (saved by Fritzing 1.0.4)
circuit board: 8.46667cm x 5.64444cm
breadboards: 1

parts:
  A1 = ESP32-S3 supermini
  A2 = GC9A01 round lcd
  A3 = GY-BMP280 Breakout
  A4 = GY-BMP280 Breakout

nets:
  N1: A1.Pin_1, A1.Pin_39, A2.Pin_6, A3.Pin_2, A4.Pin_2
  N2: A1.Pin_10, A3.Pin_3, A4.Pin_3
  N3: A1.Pin_11, A3.Pin_4, A4.Pin_4
  N4: A1.Pin_33, A2.Pin_1
  N5: A1.Pin_34, A2.Pin_2
  N6: A1.Pin_35, A2.Pin_3
  N7: A1.Pin_36, A2.Pin_4
  N8: A1.Pin_37, A2.Pin_5
  N9: A1.Pin_38, A2.Pin_7, A3.Pin_1, A4.Pin_1

custom parts:
  ESP32-S3 supermini: Esp32-S3 Development board ESP32 SuperMini development board ESP32 Development board WiFi Bluetooth.
  GC9A01 round lcd: IPS TFT display round 1.28″ 240×240 GC9A01 controller. Mar 2025 fix pcb pin with fill #ffffff instead of none. Casuses problem in etchable pcb images (pad with no hole.)
